# Fritzing sketch ArduinoScreenController-wiring-diagram (saved by Fritzing 0.7.12b)
breadboards: 1

parts:
  Arduino1 = Arduino Leonardo
  R1 = Photocell (LDR) [package=THT]
  S1 = Pushbutton [package="[SMD]"]
  S2 = Pushbutton [package="[SMD]"]

nets:
  N1: Arduino1.GND, R1.pin_0, S1.Pin_3, S1.Pin_4, S2.Pin_3, S2.Pin_4
  N2: Arduino1.A0, R1.pin_1
  N3: Arduino1.D2, Arduino1.SDA, S2.Pin_1, S2.Pin_2
  N4: Arduino1.D4, S1.Pin_1, S1.Pin_2

custom parts:
  Arduino Leonardo: The original Arduino Leonardo microcontroller
